// Digital circuit ALU.dig as structural Verilog
module ALU (
  input  [15:0] A,
  input  [15:0] B,
  input  OP_ADD,
  output [15:0] Result,
  output Carry
);

  wire _74283_1_pin9, _74283_2_pin9, _74283_3_pin9, AR0, AR1, AR2, AR3, AR4, AR5, AR6, AR7, AR8, AR9, AR10,
       AR11, AR12, AR13, AR14, AR15, NR0, NR1, NR2, NR3, NR4, NR5, NR6, NR7, NR8, NR9, NR10, NR11, NR12,
       NR13, NR14, NR15;

  _74283 _74283_1 (
    .pin1(AR1), .pin2(B[1]), .pin3(A[1]), .pin4(AR0), .pin5(A[0]), .pin6(B[0]), .pin7(1'b0), .pin8(1'b0),
    .pin9(_74283_1_pin9), .pin10(AR3), .pin11(B[3]), .pin12(A[3]), .pin13(AR2), .pin14(A[2]), .pin15(B[2]),
    .pin16(1'b1));
  _7402 _7402_1 (
    .pin1(NR0), .pin2(A[0]), .pin3(B[0]), .pin4(NR1), .pin5(A[1]), .pin6(B[1]), .pin7(1'b0), .pin8(A[2]),
    .pin9(B[2]), .pin10(NR2), .pin11(A[3]), .pin12(B[3]), .pin13(NR3), .pin14(1'b1));
  _74157 _74157_1 (
    .pin1(OP_ADD), .pin2(NR0), .pin3(AR0), .pin4(Result[0]), .pin5(NR1), .pin6(AR1), .pin7(Result[1]),
    .pin8(1'b0), .pin9(Result[2]), .pin10(AR2), .pin11(NR2), .pin12(Result[3]), .pin13(AR3), .pin14(NR3),
    .pin15(1'b0), .pin16(1'b1));
  _74283 _74283_2 (
    .pin1(AR5), .pin2(B[5]), .pin3(A[5]), .pin4(AR4), .pin5(A[4]), .pin6(B[4]), .pin7(_74283_1_pin9),
    .pin8(1'b0), .pin9(_74283_2_pin9), .pin10(AR7), .pin11(B[7]), .pin12(A[7]), .pin13(AR6), .pin14(A[6]),
    .pin15(B[6]), .pin16(1'b1));
  _7402 _7402_2 (
    .pin1(NR4), .pin2(A[4]), .pin3(B[4]), .pin4(NR5), .pin5(A[5]), .pin6(B[5]), .pin7(1'b0), .pin8(A[6]),
    .pin9(B[6]), .pin10(NR6), .pin11(A[7]), .pin12(B[7]), .pin13(NR7), .pin14(1'b1));
  _74157 _74157_2 (
    .pin1(OP_ADD), .pin2(NR4), .pin3(AR4), .pin4(Result[4]), .pin5(NR5), .pin6(AR5), .pin7(Result[5]),
    .pin8(1'b0), .pin9(Result[6]), .pin10(AR6), .pin11(NR6), .pin12(Result[7]), .pin13(AR7), .pin14(NR7),
    .pin15(1'b0), .pin16(1'b1));
  _74283 _74283_3 (
    .pin1(AR9), .pin2(B[9]), .pin3(A[9]), .pin4(AR8), .pin5(A[8]), .pin6(B[8]), .pin7(_74283_2_pin9),
    .pin8(1'b0), .pin9(_74283_3_pin9), .pin10(AR11), .pin11(B[11]), .pin12(A[11]), .pin13(AR10),
    .pin14(A[10]), .pin15(B[10]), .pin16(1'b1));
  _7402 _7402_3 (
    .pin1(NR8), .pin2(A[8]), .pin3(B[8]), .pin4(NR9), .pin5(A[9]), .pin6(B[9]), .pin7(1'b0), .pin8(A[10]),
    .pin9(B[10]), .pin10(NR10), .pin11(A[11]), .pin12(B[11]), .pin13(NR11), .pin14(1'b1));
  _74157 _74157_3 (
    .pin1(OP_ADD), .pin2(NR8), .pin3(AR8), .pin4(Result[8]), .pin5(NR9), .pin6(AR9), .pin7(Result[9]),
    .pin8(1'b0), .pin9(Result[10]), .pin10(AR10), .pin11(NR10), .pin12(Result[11]), .pin13(AR11),
    .pin14(NR11), .pin15(1'b0), .pin16(1'b1));
  _74283 _74283_4 (
    .pin1(AR13), .pin2(B[13]), .pin3(A[13]), .pin4(AR12), .pin5(A[12]), .pin6(B[12]), .pin7(_74283_3_pin9),
    .pin8(1'b0), .pin9(Carry), .pin10(AR15), .pin11(B[15]), .pin12(A[15]), .pin13(AR14), .pin14(A[14]),
    .pin15(B[14]), .pin16(1'b1));
  _7402 _7402_4 (
    .pin1(NR12), .pin2(A[12]), .pin3(B[12]), .pin4(NR13), .pin5(A[13]), .pin6(B[13]), .pin7(1'b0),
    .pin8(A[14]), .pin9(B[14]), .pin10(NR14), .pin11(A[15]), .pin12(B[15]), .pin13(NR15), .pin14(1'b1));
  _74157 _74157_4 (
    .pin1(OP_ADD), .pin2(NR12), .pin3(AR12), .pin4(Result[12]), .pin5(NR13), .pin6(AR13), .pin7(Result[13]),
    .pin8(1'b0), .pin9(Result[14]), .pin10(AR14), .pin11(NR14), .pin12(Result[15]), .pin13(AR15),
    .pin14(NR15), .pin15(1'b0), .pin16(1'b1));

  // Other names for the same wires on the sheet: Carry_Flag = Carry; R0 = Result[0]; R1 = Result[1]; R2 = Result[2];
  //   R3 = Result[3]; R4 = Result[4]; R5 = Result[5]; R6 = Result[6]; R7 = Result[7]; R8 = Result[8]; R9 = Result[9];
  //   R10 = Result[10]; R11 = Result[11]; R12 = Result[12]; R13 = Result[13]; R14 = Result[14]; R15 = Result[15]
endmodule
