// Digital circuit DemoDevice.dig as structural Verilog
module DemoDevice (
  input  Reset,
  input  [15:0] D_In,
  input  Clock,
  input  DO_STA,
  input  IR_BIT0,
  input  nEnable,
  input  IR_BIT1,
  output [3:0] D1,
  output [3:0] D2,
  output [3:0] D3,
  output [3:0] D4,
  output LED1
);

  wire _7404_1_pin6, _7404_1_pin8, _7404_1_pin11, _7408_1_pin6, _7408_1_pin8, _7408_1_pin10, _7408_1_pin13,
       _7408_2_pin3, _7408_2_pin6, _7408_2_pin9, _7408_2_pin10, _7408_2_pin12, _7408_2_pin13, _74173_1_pin11,
       _74173_1_pin12, _74173_1_pin13, Enable, nIR_BIT0, notconnected_1_out, notconnected_2_out;

  // NotConnected on notconnected_1_out
  // NotConnected on notconnected_2_out
  _7408 _7408_1 (
    .pin1(notconnected_1_out), .pin2(notconnected_2_out), .pin4(Enable), .pin5(DO_STA), .pin6(_7408_1_pin6),
    .pin7(1'b0), .pin8(_7408_1_pin8), .pin9(_7408_1_pin6), .pin10(_7408_1_pin10), .pin11(_7408_1_pin10),
    .pin12(IR_BIT0), .pin13(_7408_1_pin13), .pin14(1'b1));  // open: pin3
  _7408 _7408_2 (
    .pin1(IR_BIT1), .pin2(nIR_BIT0), .pin3(_7408_2_pin3), .pin4(_7408_2_pin3), .pin5(_7408_1_pin6),
    .pin6(_7408_2_pin6), .pin7(1'b0), .pin9(_7408_2_pin9), .pin10(_7408_2_pin10), .pin12(_7408_2_pin12),
    .pin13(_7408_2_pin13), .pin14(1'b1));  // open: pin8, pin11
  // NotConnected on _7408_2_pin13
  // NotConnected on _7408_2_pin12
  // NotConnected on _7408_2_pin10
  // NotConnected on _7408_2_pin9
  _7404 _7404_1 (
    .pin1(IR_BIT1), .pin2(_7408_1_pin13), .pin3(IR_BIT0), .pin4(nIR_BIT0), .pin5(_7408_1_pin8),
    .pin6(_7404_1_pin6), .pin7(1'b0), .pin8(_7404_1_pin8), .pin9(_7408_2_pin6), .pin11(_7404_1_pin11),
    .pin12(Enable), .pin13(nEnable), .pin14(1'b1));  // open: pin10
  Register register_1 (.Reset(Reset), .D_In(D_In), .nWrite(_7404_1_pin6), .Clock(Clock), .D_Out({D4, D3, D2, D1}));
  // NotConnected on _7404_1_pin11
  _74173 _74173_1 (
    .pin1(1'b0), .pin2(1'b0), .pin3(LED1), .pin7(Clock), .pin8(1'b0), .pin9(_7404_1_pin8),
    .pin10(_7404_1_pin8), .pin11(_74173_1_pin11), .pin12(_74173_1_pin12), .pin13(_74173_1_pin13),
    .pin14(D_In[0]), .pin15(Reset), .pin16(1'b1));  // open: pin4, pin5, pin6
  // NotConnected on _74173_1_pin13
  // NotConnected on _74173_1_pin12
  // NotConnected on _74173_1_pin11

  // Other names for the same wires on the sheet: DATA_BIT0 = D_In[0]; DATA_IN[15:0] = D_In;
  //   DATA_OUT[15:0] = {D4, D3, D2, D1}; R0 = LED1
endmodule
