// Digital circuit Multiplexer.dig as structural Verilog
module Multiplexer (
  input  [15:0] A,
  input  [15:0] B,
  input  Select,
  output [15:0] Result
);

  _74157 _74157_1 (
    .pin1(Select), .pin2(A[0]), .pin3(B[0]), .pin4(Result[0]), .pin5(A[1]), .pin6(B[1]), .pin7(Result[1]),
    .pin8(1'b0), .pin9(Result[2]), .pin10(B[2]), .pin11(A[2]), .pin12(Result[3]), .pin13(B[3]), .pin14(A[3]),
    .pin15(1'b0), .pin16(1'b1));
  _74157 _74157_2 (
    .pin1(Select), .pin2(A[4]), .pin3(B[4]), .pin4(Result[4]), .pin5(A[5]), .pin6(B[5]), .pin7(Result[5]),
    .pin8(1'b0), .pin9(Result[6]), .pin10(B[6]), .pin11(A[6]), .pin12(Result[7]), .pin13(B[7]), .pin14(A[7]),
    .pin15(1'b0), .pin16(1'b1));
  _74157 _74157_3 (
    .pin1(Select), .pin2(A[8]), .pin3(B[8]), .pin4(Result[8]), .pin5(A[9]), .pin6(B[9]), .pin7(Result[9]),
    .pin8(1'b0), .pin9(Result[10]), .pin10(B[10]), .pin11(A[10]), .pin12(Result[11]), .pin13(B[11]),
    .pin14(A[11]), .pin15(1'b0), .pin16(1'b1));
  _74157 _74157_4 (
    .pin1(Select), .pin2(A[12]), .pin3(B[12]), .pin4(Result[12]), .pin5(A[13]), .pin6(B[13]),
    .pin7(Result[13]), .pin8(1'b0), .pin9(Result[14]), .pin10(B[14]), .pin11(A[14]), .pin12(Result[15]),
    .pin13(B[15]), .pin14(A[15]), .pin15(1'b0), .pin16(1'b1));

  // Other names for the same wires on the sheet: R0 = Result[0]; R1 = Result[1]; R2 = Result[2]; R3 = Result[3];
  //   R4 = Result[4]; R5 = Result[5]; R6 = Result[6]; R7 = Result[7]; R8 = Result[8]; R9 = Result[9];
  //   R10 = Result[10]; R11 = Result[11]; R12 = Result[12]; R13 = Result[13]; R14 = Result[14]; R15 = Result[15];
  //   Sel = Select
endmodule
