// Digital circuit OutputBuffer.dig as structural Verilog
module OutputBuffer (
  input  [15:0] IN,
  input  nOE,
  output [15:0] OUT
);

  _74245 _74245_1 (
    .pin1(1'b1), .pin2(IN[0]), .pin3(IN[1]), .pin4(IN[2]), .pin5(IN[3]), .pin6(IN[4]), .pin7(IN[5]),
    .pin8(IN[6]), .pin9(IN[7]), .pin10(1'b0), .pin11(OUT[7]), .pin12(OUT[6]), .pin13(OUT[5]), .pin14(OUT[4]),
    .pin15(OUT[3]), .pin16(OUT[2]), .pin17(OUT[1]), .pin18(OUT[0]), .pin19(nOE), .pin20(1'b1));
  _74245 _74245_2 (
    .pin1(1'b1), .pin2(IN[8]), .pin3(IN[9]), .pin4(IN[10]), .pin5(IN[11]), .pin6(IN[12]), .pin7(IN[13]),
    .pin8(IN[14]), .pin9(IN[15]), .pin10(1'b0), .pin11(OUT[15]), .pin12(OUT[14]), .pin13(OUT[13]),
    .pin14(OUT[12]), .pin15(OUT[11]), .pin16(OUT[10]), .pin17(OUT[9]), .pin18(OUT[8]), .pin19(nOE),
    .pin20(1'b1));

  // Other names for the same wires on the sheet: A0 = IN[0]; A1 = IN[1]; A2 = IN[2]; A3 = IN[3]; A4 = IN[4];
  //   A5 = IN[5]; A6 = IN[6]; A7 = IN[7]; A8 = IN[8]; A9 = IN[9]; A10 = IN[10]; A11 = IN[11]; A12 = IN[12];
  //   A13 = IN[13]; A14 = IN[14]; A15 = IN[15]; R0 = OUT[0]; R1 = OUT[1]; R2 = OUT[2]; R3 = OUT[3]; R4 = OUT[4];
  //   R5 = OUT[5]; R6 = OUT[6]; R7 = OUT[7]; R8 = OUT[8]; R9 = OUT[9]; R10 = OUT[10]; R11 = OUT[11]; R12 = OUT[12];
  //   R13 = OUT[13]; R14 = OUT[14]; R15 = OUT[15]
endmodule
