// Digital circuit ProgramCounter.dig as structural Verilog
module ProgramCounter (
  input  Clock,
  input  nReset,
  input  nLoad,
  input  Enable,
  input  [15:0] Addr,
  output [15:0] PC
);

  wire _74161_1_pin15, _74161_2_pin15, _74161_3_pin15;

  _74161 _74161_1 (
    .pin1(nReset), .pin2(Clock), .pin3(Addr[0]), .pin4(Addr[1]), .pin5(Addr[2]), .pin6(Addr[3]),
    .pin7(Enable), .pin8(1'b0), .pin9(nLoad), .pin10(Enable), .pin11(PC[3]), .pin12(PC[2]), .pin13(PC[1]),
    .pin14(PC[0]), .pin15(_74161_1_pin15), .pin16(1'b1));
  _74161 _74161_2 (
    .pin1(nReset), .pin2(Clock), .pin3(Addr[4]), .pin4(Addr[5]), .pin5(Addr[6]), .pin6(Addr[7]),
    .pin7(Enable), .pin8(1'b0), .pin9(nLoad), .pin10(_74161_1_pin15), .pin11(PC[7]), .pin12(PC[6]),
    .pin13(PC[5]), .pin14(PC[4]), .pin15(_74161_2_pin15), .pin16(1'b1));
  _74161 _74161_3 (
    .pin1(nReset), .pin2(Clock), .pin3(Addr[8]), .pin4(Addr[9]), .pin5(Addr[10]), .pin6(Addr[11]),
    .pin7(Enable), .pin8(1'b0), .pin9(nLoad), .pin10(_74161_2_pin15), .pin11(PC[11]), .pin12(PC[10]),
    .pin13(PC[9]), .pin14(PC[8]), .pin15(_74161_3_pin15), .pin16(1'b1));
  _74161 _74161_4 (
    .pin1(nReset), .pin2(Clock), .pin3(Addr[12]), .pin4(Addr[13]), .pin5(Addr[14]), .pin6(Addr[15]),
    .pin7(Enable), .pin8(1'b0), .pin9(nLoad), .pin10(_74161_3_pin15), .pin11(PC[15]), .pin12(PC[14]),
    .pin13(PC[13]), .pin14(PC[12]), .pin16(1'b1));  // open: pin15

  // Other names for the same wires on the sheet: Bus0 = Addr[0]; Bus1 = Addr[1]; Bus2 = Addr[2]; Bus3 = Addr[3];
  //   Bus4 = Addr[4]; Bus5 = Addr[5]; Bus6 = Addr[6]; Bus7 = Addr[7]; Bus8 = Addr[8]; Bus9 = Addr[9];
  //   Bus10 = Addr[10]; Bus11 = Addr[11]; Bus12 = Addr[12]; Bus13 = Addr[13]; Bus14 = Addr[14]; Bus15 = Addr[15];
  //   Addr0 = PC[0]; Addr1 = PC[1]; Addr2 = PC[2]; Addr3 = PC[3]; Addr4 = PC[4]; Addr5 = PC[5]; Addr6 = PC[6];
  //   Addr7 = PC[7]; Addr8 = PC[8]; Addr9 = PC[9]; Addr10 = PC[10]; Addr11 = PC[11]; Addr12 = PC[12]; Addr13 = PC[13];
  //   Addr14 = PC[14]; Addr15 = PC[15]

  // Notes on the sheet:
  //   Clock: Hz: 5
endmodule
