// Digital circuit RAM.dig as structural Verilog
module RAM (
  input  nOE,
  input  nWE,
  input  [15:0] Address,
  input  [15:0] Data,
  input  nCE
);

  wire D0, D1, D2, D3, D4, D5, D6, D7, D8, D9, D10, D11, D12, D13, D14, D15, not_1_out;

  not not_1 (not_1_out, nOE);
  BusSplitter #(.Bits(16)) bussplitter_1 (
    .D(Data), .OE(not_1_out), .D0(D0), .D1(D1), .D2(D2), .D3(D3), .D4(D4), .D5(D5), .D6(D6), .D7(D7),
    .D8(D8), .D9(D9), .D10(D10), .D11(D11), .D12(D12), .D13(D13), .D14(D14), .D15(D15));
  // A623308A a623308a_1: pin names not known; wires that end beside it: Address[12], Address[7], Address[6], Address[5], Address[4], Address[3], Address[2], Address[1], Address[0], D0, D1, D2, 1'b0, 1'b1, nWE, Address[8], Address[9], Address[11], nOE, Address[10], nCE, D7
  // A623308A a623308a_2: pin names not known; wires that end beside it: Address[12], Address[7], Address[6], Address[5], Address[4], Address[3], Address[2], Address[1], Address[0], D8, D9, D10, 1'b0, 1'b1, nWE, Address[8], Address[9], Address[11], nOE, Address[10], nCE, D15

  // Other names for the same wires on the sheet: A0 = Address[0]; A1 = Address[1]; A2 = Address[2]; A3 = Address[3];
  //   A4 = Address[4]; A5 = Address[5]; A6 = Address[6]; A7 = Address[7]; A8 = Address[8]; A9 = Address[9];
  //   A10 = Address[10]; A11 = Address[11]; A12 = Address[12]; A13 = Address[13]; A14 = Address[14];
  //   A15 = Address[15]
endmodule
