// Digital circuit Register.dig as structural Verilog
module Register (
  input  Reset,
  input  [15:0] D_In,
  input  nWrite,
  input  Clock,
  output [15:0] D_Out
);

  _74173 _74173_1 (
    .pin1(1'b0), .pin2(1'b0), .pin3(D_Out[0]), .pin4(D_Out[1]), .pin5(D_Out[2]), .pin6(D_Out[3]),
    .pin7(Clock), .pin8(1'b0), .pin9(nWrite), .pin10(nWrite), .pin11(D_In[3]), .pin12(D_In[2]),
    .pin13(D_In[1]), .pin14(D_In[0]), .pin15(Reset), .pin16(1'b1));
  _74173 _74173_2 (
    .pin1(1'b0), .pin2(1'b0), .pin3(D_Out[4]), .pin4(D_Out[5]), .pin5(D_Out[6]), .pin6(D_Out[7]),
    .pin7(Clock), .pin8(1'b0), .pin9(nWrite), .pin10(nWrite), .pin11(D_In[7]), .pin12(D_In[6]),
    .pin13(D_In[5]), .pin14(D_In[4]), .pin15(Reset), .pin16(1'b1));
  _74173 _74173_3 (
    .pin1(1'b0), .pin2(1'b0), .pin3(D_Out[8]), .pin4(D_Out[9]), .pin5(D_Out[10]), .pin6(D_Out[11]),
    .pin7(Clock), .pin8(1'b0), .pin9(nWrite), .pin10(nWrite), .pin11(D_In[11]), .pin12(D_In[10]),
    .pin13(D_In[9]), .pin14(D_In[8]), .pin15(Reset), .pin16(1'b1));
  _74173 _74173_4 (
    .pin1(1'b0), .pin2(1'b0), .pin3(D_Out[12]), .pin4(D_Out[13]), .pin5(D_Out[14]), .pin6(D_Out[15]),
    .pin7(Clock), .pin8(1'b0), .pin9(nWrite), .pin10(nWrite), .pin11(D_In[15]), .pin12(D_In[14]),
    .pin13(D_In[13]), .pin14(D_In[12]), .pin15(Reset), .pin16(1'b1));

  // Other names for the same wires on the sheet: D0 = D_In[0]; D1 = D_In[1]; D2 = D_In[2]; D3 = D_In[3]; D4 = D_In[4];
  //   D5 = D_In[5]; D6 = D_In[6]; D7 = D_In[7]; D8 = D_In[8]; D9 = D_In[9]; D10 = D_In[10]; D11 = D_In[11];
  //   D12 = D_In[12]; D13 = D_In[13]; D14 = D_In[14]; D15 = D_In[15]; nWR = nWrite; R0 = D_Out[0]; R1 = D_Out[1];
  //   R2 = D_Out[2]; R3 = D_Out[3]; R4 = D_Out[4]; R5 = D_Out[5]; R6 = D_Out[6]; R7 = D_Out[7]; R8 = D_Out[8];
  //   R9 = D_Out[9]; R10 = D_Out[10]; R11 = D_Out[11]; R12 = D_Out[12]; R13 = D_Out[13]; R14 = D_Out[14];
  //   R15 = D_Out[15]
endmodule
