// Digital circuit Register2.dig as structural Verilog
module Register2 (
  input  nReset,
  input  [15:0] D_In,
  input  Write,
  output [15:0] D_Out
);

  _74273 _74273_1 (
    .pin1(nReset), .pin2(D_Out[0]), .pin3(D_In[0]), .pin4(D_In[1]), .pin5(D_Out[1]), .pin6(D_Out[2]),
    .pin7(D_In[2]), .pin8(D_In[3]), .pin9(D_Out[3]), .pin10(1'b0), .pin11(Write), .pin12(D_Out[4]),
    .pin13(D_In[4]), .pin14(D_In[5]), .pin15(D_Out[5]), .pin16(D_Out[6]), .pin17(D_In[6]), .pin18(D_In[7]),
    .pin19(D_Out[7]), .pin20(1'b1));
  _74273 _74273_2 (
    .pin1(nReset), .pin2(D_Out[8]), .pin3(D_In[8]), .pin4(D_In[9]), .pin5(D_Out[9]), .pin6(D_Out[10]),
    .pin7(D_In[10]), .pin8(D_In[11]), .pin9(D_Out[11]), .pin10(1'b0), .pin11(Write), .pin12(D_Out[12]),
    .pin13(D_In[12]), .pin14(D_In[13]), .pin15(D_Out[13]), .pin16(D_Out[14]), .pin17(D_In[14]),
    .pin18(D_In[15]), .pin19(D_Out[15]), .pin20(1'b1));

  // Other names for the same wires on the sheet: D0 = D_In[0]; D1 = D_In[1]; D2 = D_In[2]; D3 = D_In[3]; D4 = D_In[4];
  //   D5 = D_In[5]; D6 = D_In[6]; D7 = D_In[7]; D8 = D_In[8]; D9 = D_In[9]; D10 = D_In[10]; D11 = D_In[11];
  //   D12 = D_In[12]; D13 = D_In[13]; D14 = D_In[14]; D15 = D_In[15]; R0 = D_Out[0]; R1 = D_Out[1]; R2 = D_Out[2];
  //   R3 = D_Out[3]; R4 = D_Out[4]; R5 = D_Out[5]; R6 = D_Out[6]; R7 = D_Out[7]; R8 = D_Out[8]; R9 = D_Out[9];
  //   R10 = D_Out[10]; R11 = D_Out[11]; R12 = D_Out[12]; R13 = D_Out[13]; R14 = D_Out[14]; R15 = D_Out[15];
  //   WR = Write
endmodule
