// Digital circuit SCPU.dig as structural Verilog
module SCPU (
  input  Clock,
  input  Reset
);

  wire _7404_1_pin1, _7404_1_pin3, _7404_1_pin5, _7404_1_pin9, _74107_1_pin12, _74157_1_pin2, _74157_1_pin3,
       _74157_1_pin5, _74157_1_pin6, _74245_2_pin11, _74245_2_pin12, _74245_2_pin13, _74245_2_pin14,
       _74245_2_pin15, _74245_2_pin16, _74245_2_pin17, _74245_2_pin18, ADDR0, ADDR1, ADDR2, CARRY,
       CARRY_FLAG, CARRY_WE, CF_ADDR, DO_STA, EXT_IO, Fetch_IR, IMMEDIATE, INDIRECTION, IODEV_SCPU, nACCU_WE,
       nADDR0, nADDR1, nADDR2, nCF_RESET, nDevice0, nDevice1, nDevice2, nDevice3, nDO_JMP, nDO_STA,
       nFetch_IR, nINDIRECT_RESET, nINDIRECTED, nINDIRECTION, nIO0, nIO1, nIO2, nIODEV_SCPU, nOP0, nOP1,
       nOP_JMP, nTTL_OUT, OP_ADD, OP_STA, RAM_EN, RAM_MODE, RAM_STA, Reset_t, ROM_EN, S0, S1, U1_pin9,
       U2_pin3, U2_pin10, U3_pin3, U3_pin6, U4_pin4, U4_pin5, U4_pin10, U12_pin2, U12_pin3, U12_pin5,
       U12_pin6, U12_pin9, U12_pin10, U12_pin11, U12_pin13, U12_pin14, U13_pin1, U13_pin2, U13_pin4,
       U13_pin5, U14_pin3, U14_pin9, U14_pin10, U14_pin11, U16_pin6, U16_pin8, U17_pin3, U17_pin5, U19_pin2,
       U19_pin10, U20_2_pin3, U20_2_pin9, U20_2_pin10, U21_2_pin1, U21_2_pin2, U21_2_pin4, U21_2_pin5,
       U21_2_pin8, U21_2_pin10, U21_pin1, U21_pin2, U21_pin3, U21_pin4, U21_pin11, U24_pin3, U24_pin4,
       U24_pin5, U24_pin6, U24_pin9;
  wire [2:0] IO_DEVICE;
  wire [3:0] demodevice_1_d1, demodevice_1_d2, demodevice_1_d3, demodevice_1_d4;
  wire [15:0] Accumulator_d_out, ALU_OP, ALU_result, BUS_Data, IR, PC, ROM_Address_result;
  wire [15:14] Next_IR;

  _7404 U1 (
    .pin1(ADDR0), .pin2(nADDR0), .pin3(ADDR1), .pin4(nADDR1), .pin5(ADDR2), .pin6(nADDR2), .pin7(1'b0),
    .pin9(U1_pin9), .pin10(nOP1), .pin11(IR[14]), .pin12(nOP0), .pin13(IR[15]), .pin14(1'b1));  // open: pin8
  _7432 U19 (
    .pin1(CARRY), .pin2(U19_pin2), .pin3(nDO_JMP), .pin4(S0), .pin5(nOP_JMP), .pin6(U19_pin2), .pin7(1'b0),
    .pin8(nOP_JMP), .pin9(INDIRECTION), .pin10(U19_pin10), .pin11(U19_pin10), .pin12(nOP1), .pin13(nOP0),
    .pin14(1'b1));
  _7408 U3 (
    .pin1(ADDR0), .pin2(ADDR1), .pin3(U3_pin3), .pin4(ADDR0), .pin5(nADDR1), .pin6(U3_pin6), .pin7(1'b0),
    .pin8(INDIRECTION), .pin9(ADDR2), .pin10(U3_pin3), .pin11(IMMEDIATE), .pin12(nADDR2), .pin13(U3_pin3),
    .pin14(1'b1));
  _74107 _74107_1 (
    .pin1(1'b1), .pin2(S0), .pin3(S1), .pin4(1'b1), .pin7(1'b0), .pin8(1'b0), .pin9(1'b0), .pin10(1'b0),
    .pin11(1'b0), .pin12(_74107_1_pin12), .pin13(Reset), .pin14(1'b1));  // open: pin5, pin6
  ALU ALU (.A(Accumulator_d_out), .B(ALU_OP), .OP_ADD(OP_ADD), .Result(ALU_result), .Carry(CARRY_FLAG));
  Register Accumulator (
    .Reset(Reset_t), .D_In(ALU_result), .nWrite(nACCU_WE), .Clock(Clock), .D_Out(Accumulator_d_out));
  Multiplexer u_ALU_Op (.A(BUS_Data), .B({{5{1'b0}}, IO_DEVICE, IR[7:0]}), .Select(IMMEDIATE), .Result(ALU_OP));
  // NotConnected on U1_pin9
  _7404 _7404_1 (
    .pin1(_7404_1_pin1), .pin3(_7404_1_pin3), .pin5(_7404_1_pin5), .pin7(1'b0), .pin9(_7404_1_pin9),
    .pin10(Reset_t), .pin11(Reset), .pin12(_74107_1_pin12), .pin13(Clock), .pin14(1'b1));  // open: pin2, pin4, pin6, pin8
  // NotConnected on _7404_1_pin1
  // Probe on ALU_OP
  _7404 U17 (
    .pin1(nIODEV_SCPU), .pin2(IODEV_SCPU), .pin3(U17_pin3), .pin5(U17_pin5), .pin7(1'b0), .pin8(nFetch_IR),
    .pin9(Fetch_IR), .pin10(nINDIRECTION), .pin11(INDIRECTION), .pin12(nDO_STA), .pin13(DO_STA), .pin14(1'b1));  // open: pin4, pin6
  _7432 U16 (
    .pin1(S0), .pin2(nINDIRECTED), .pin3(nINDIRECT_RESET), .pin4(INDIRECTION), .pin5(RAM_MODE),
    .pin6(U16_pin6), .pin7(1'b0), .pin8(U16_pin8), .pin9(S1), .pin10(nOP_JMP), .pin11(ROM_EN),
    .pin12(Fetch_IR), .pin13(nADDR0), .pin14(1'b1));
  _7408 U4 (
    .pin1(U3_pin6), .pin2(nADDR2), .pin3(RAM_MODE), .pin4(U4_pin4), .pin5(U4_pin5), .pin7(1'b0),
    .pin8(EXT_IO), .pin9(S1), .pin10(U4_pin10), .pin11(U4_pin10), .pin12(ADDR2), .pin13(U3_pin6), .pin14(1'b1));  // open: pin6
  // NotConnected on _7404_1_pin3
  // NotConnected on U17_pin3
  // NotConnected on U4_pin4
  // NotConnected on _7404_1_pin5
  OutputBuffer Buffer (.IN(Accumulator_d_out), .nOE(nDO_STA), .OUT(BUS_Data));
  // NotConnected on U17_pin5
  // NotConnected on U4_pin5
  // NotConnected on _7404_1_pin9
  _7408 U2 (
    .pin1(nOP0), .pin2(IR[14]), .pin3(U2_pin3), .pin4(U2_pin3), .pin5(nINDIRECTION), .pin6(OP_ADD),
    .pin7(1'b0), .pin8(OP_STA), .pin9(nINDIRECTION), .pin10(U2_pin10), .pin11(U2_pin10), .pin12(IR[15]),
    .pin13(nOP1), .pin14(1'b1));
  _7408 U18 (
    .pin1(U16_pin6), .pin2(nFetch_IR), .pin3(RAM_EN), .pin4(OP_STA), .pin5(S1), .pin6(DO_STA), .pin7(1'b0),
    .pin8(RAM_STA), .pin9(RAM_EN), .pin10(DO_STA), .pin11(nCF_RESET), .pin12(Reset), .pin13(U16_pin8),
    .pin14(1'b1));
  ProgramCounter Program_Counter (
    .Clock(Clock), .nReset(Reset), .nLoad(nDO_JMP), .Enable(Fetch_IR), .Addr(ALU_OP), .PC(PC));
  Register Instruction_Register (
    .Reset(Reset_t), .D_In({Next_IR, BUS_Data[13:0]}), .nWrite(S1), .Clock(Clock),
    .D_Out({IR[15:14], ADDR0, ADDR1, ADDR2, IO_DEVICE, IR[7:0]}));
  _74157 U12 (
    .pin1(CARRY_WE), .pin2(U12_pin2), .pin3(U12_pin3), .pin5(U12_pin5), .pin6(U12_pin6), .pin8(1'b0),
    .pin9(U12_pin9), .pin10(U12_pin10), .pin11(U12_pin11), .pin13(U12_pin13), .pin14(U12_pin14),
    .pin15(1'b0), .pin16(1'b1));  // open: pin4, pin7, pin12
  // NotConnected on U12_pin14
  // NotConnected on U12_pin2
  // NotConnected on U12_pin3
  // Probe on PC
  // Probe on {IR[15:14], ADDR0, ADDR1, ADDR2, IO_DEVICE, IR[7:0]}
  // NotConnected on U12_pin13
  // NotConnected on U12_pin5
  // NotConnected on U12_pin6
  _7474 U21 (
    .pin1(U21_pin1), .pin2(U21_pin2), .pin3(U21_pin3), .pin4(U21_pin4), .pin7(1'b0), .pin8(nINDIRECTED),
    .pin10(1'b1), .pin11(U21_pin11), .pin12(INDIRECTION), .pin13(nINDIRECT_RESET), .pin14(1'b1));  // open: pin5, pin6, pin9
  // NotConnected on U21_pin1
  _7432 U14 (
    .pin1(S0), .pin2(IR[15]), .pin3(U14_pin3), .pin4(U14_pin3), .pin5(INDIRECTION), .pin6(nACCU_WE),
    .pin7(1'b0), .pin8(CARRY_WE), .pin9(U14_pin9), .pin10(U14_pin10), .pin11(U14_pin11), .pin12(CF_ADDR),
    .pin13(CARRY_FLAG), .pin14(1'b1));
  // NotConnected on U21_pin2
  // NotConnected on U21_pin3
  Multiplexer ROM_Address (
    .A({3'b000, ADDR1, ADDR2, IO_DEVICE, IR[7:0]}), .B(PC), .Select(S0), .Result(ROM_Address_result));
  // NotConnected on U21_pin4
  _74138 U22 (
    .pin1(IO_DEVICE[0]), .pin2(IO_DEVICE[1]), .pin3(IO_DEVICE[2]), .pin4(1'b0), .pin5(1'b0), .pin6(EXT_IO),
    .pin7(nIODEV_SCPU), .pin8(1'b0), .pin12(nDevice3), .pin13(nDevice2), .pin14(nDevice1), .pin15(nDevice0),
    .pin16(1'b1));  // open: pin9, pin10, pin11
  // Probe on ROM_Address_result
  RAMSinglePortSel #(.AddrBits(16), .Bits(16)) RAM (
    .A({{5{1'b0}}, IO_DEVICE, IR[7:0]}), .CS(RAM_EN), .WE(RAM_STA), .OE(nDO_STA), .D(BUS_Data));
  EEPROM #(.AddrBits(16), .isProgramMemory("true"), .Bits(16)) ROM (
    .A(ROM_Address_result), .CS(ROM_EN), .WE(1'b0), .OE(nDO_STA), .D(BUS_Data));
  _7408 U13 (
    .pin1(U13_pin1), .pin2(U13_pin2), .pin4(U13_pin4), .pin5(U13_pin5), .pin7(1'b0), .pin8(Fetch_IR),
    .pin9(S0), .pin10(nINDIRECTED), .pin11(U21_pin11), .pin12(S1), .pin13(Clock), .pin14(1'b1));  // open: pin3, pin6
  // NotConnected on U13_pin1
  // NotConnected on U13_pin2
  _7408 U15 (
    .pin1(OP_ADD), .pin2(S1), .pin3(U14_pin9), .pin4(CF_ADDR), .pin5(DO_STA), .pin6(U14_pin10), .pin7(1'b0),
    .pin8(CF_ADDR), .pin9(IODEV_SCPU), .pin10(IR[0]), .pin11(U12_pin10), .pin12(U14_pin11), .pin13(CARRY_WE),
    .pin14(1'b1));
  // NotConnected on U13_pin4
  // NotConnected on U13_pin5
  // Probe on BUS_Data
  _74138 U23 (
    .pin1(IR[0]), .pin2(IR[1]), .pin3(IR[2]), .pin4(1'b0), .pin5(1'b0), .pin6(1'b1), .pin8(1'b0),
    .pin13(nIO2), .pin14(nIO1), .pin15(nIO0), .pin16(1'b1));  // open: pin7, pin9, pin10, pin11, pin12
  _74157 _74157_1 (
    .pin1(INDIRECTION), .pin2(_74157_1_pin2), .pin3(_74157_1_pin3), .pin5(_74157_1_pin5),
    .pin6(_74157_1_pin6), .pin8(1'b0), .pin9(Next_IR[14]), .pin10(IR[14]), .pin11(BUS_Data[14]),
    .pin12(Next_IR[15]), .pin13(IR[15]), .pin14(BUS_Data[15]), .pin15(1'b0), .pin16(1'b1));  // open: pin4, pin7
  _7474 U20 (
    .pin1(1'b1), .pin2(U12_pin9), .pin3(Clock), .pin4(1'b1), .pin5(U12_pin11), .pin7(1'b0), .pin9(CARRY),
    .pin10(1'b1), .pin11(Clock), .pin12(U12_pin11), .pin13(nCF_RESET), .pin14(1'b1));  // open: pin6, pin8
  // NotConnected on _74157_1_pin2
  // NotConnected on _74157_1_pin3
  // NotConnected on _74157_1_pin5
  // NotConnected on _74157_1_pin6
  // Probe on {Next_IR, BUS_Data[13:0]}
  DemoDevice demodevice_1 (
    .Reset(Reset_t), .D_In(BUS_Data), .Clock(Clock), .DO_STA(DO_STA), .IR_BIT0(IR[0]), .nEnable(nDevice0),
    .IR_BIT1(IR[1]), .D1(demodevice_1_d1), .D2(demodevice_1_d2), .D3(demodevice_1_d3), .D4(demodevice_1_d4));  // open: LED1
  _74173 U24 (
    .pin1(1'b0), .pin2(1'b0), .pin3(U24_pin3), .pin4(U24_pin4), .pin5(U24_pin5), .pin6(U24_pin6),
    .pin7(Clock), .pin8(1'b0), .pin9(U24_pin9), .pin10(nDevice0), .pin11(BUS_Data[0]), .pin12(BUS_Data[1]),
    .pin13(BUS_Data[2]), .pin14(BUS_Data[3]), .pin15(Reset_t), .pin16(1'b1));
  LED led_1 (.in(U24_pin3));
  LED led_2 (.in(U24_pin4));
  LED led_3 (.in(U24_pin5));
  LED led_4 (.in(U24_pin6));
  // TerminalDevice terminaldevice_1: pin names not known; wires that end beside it: Reset_t, BUS_Data, Clock, DO_STA, IR[0], nDevice1, IR[1], BUS_Data
  Seven_Seg_Hex seven_seg_hex_1 (.d(demodevice_1_d4), .dp(1'b0));
  Seven_Seg_Hex seven_seg_hex_2 (.d(demodevice_1_d3), .dp(1'b0));
  _7432 U20_2 (
    .pin1(nIO1), .pin2(nDO_STA), .pin3(U20_2_pin3), .pin4(U20_2_pin3), .pin5(nDevice1), .pin6(nTTL_OUT),
    .pin7(1'b0), .pin9(U20_2_pin9), .pin10(U20_2_pin10), .pin11(U24_pin9), .pin12(nIO2), .pin13(nDO_STA),
    .pin14(1'b1));  // open: pin8
  Seven_Seg_Hex seven_seg_hex_3 (.d(demodevice_1_d2), .dp(1'b0));
  Seven_Seg_Hex seven_seg_hex_4 (.d(demodevice_1_d1), .dp(1'b0));
  // NotConnected on U20_2_pin10
  // NotConnected on U20_2_pin9
  _7432 U21_2 (
    .pin1(U21_2_pin1), .pin2(U21_2_pin2), .pin4(U21_2_pin4), .pin5(U21_2_pin5), .pin7(1'b0),
    .pin8(U21_2_pin8), .pin9(DO_STA), .pin10(U21_2_pin10), .pin11(U21_2_pin10), .pin12(nIO1),
    .pin13(nDevice3), .pin14(1'b1));  // open: pin3, pin6
  // NotConnected on U21_2_pin1
  // NotConnected on U21_2_pin2
  // NotConnected on U21_2_pin4
  // NotConnected on U21_2_pin5
  _74245 _74245_1 (
    .pin1(1'b0), .pin2(BUS_Data[15]), .pin3(BUS_Data[14]), .pin4(BUS_Data[13]), .pin5(BUS_Data[12]),
    .pin6(BUS_Data[11]), .pin7(BUS_Data[10]), .pin8(BUS_Data[9]), .pin9(BUS_Data[8]), .pin10(1'b0),
    .pin11(1'b0), .pin12(1'b0), .pin13(1'b0), .pin14(1'b0), .pin15(1'b0), .pin16(1'b0), .pin17(1'b0),
    .pin18(1'b0), .pin19(U21_2_pin8), .pin20(1'b1));
  _74245 _74245_2 (
    .pin1(1'b0), .pin2(BUS_Data[7]), .pin3(BUS_Data[6]), .pin4(BUS_Data[5]), .pin5(BUS_Data[4]),
    .pin6(BUS_Data[3]), .pin7(BUS_Data[2]), .pin8(BUS_Data[1]), .pin9(BUS_Data[0]), .pin10(1'b0),
    .pin11(_74245_2_pin11), .pin12(_74245_2_pin12), .pin13(_74245_2_pin13), .pin14(_74245_2_pin14),
    .pin15(_74245_2_pin15), .pin16(_74245_2_pin16), .pin17(_74245_2_pin17), .pin18(_74245_2_pin18),
    .pin19(U21_2_pin8), .pin20(1'b1));
  DipSwitch dipswitch_1 (.out(_74245_2_pin18));
  DipSwitch dipswitch_2 (.out(_74245_2_pin16));
  DipSwitch dipswitch_3 (.out(_74245_2_pin17));
  Button button_1 (.out(_74245_2_pin14));
  DipSwitch dipswitch_4 (.out(_74245_2_pin15));
  Button button_2 (.out(_74245_2_pin12));
  Button button_3 (.out(_74245_2_pin13));
  Button button_4 (.out(_74245_2_pin11));

  // Other names for the same wires on the sheet: Next_IR[13:0] = BUS_Data[13:0]; IR_11b[10:0] = {IO_DEVICE, IR[7:0]};
  //   IR_13b[12:0] = {ADDR1, ADDR2, IO_DEVICE, IR[7:0]}; IR_BIT0 = IR[0]; IR_BIT1 = IR[1]; IR_BIT2 = IR[2];
  //   IODEV_BIT2 = IO_DEVICE[0]; IR[13:8] = {ADDR0, ADDR1, ADDR2, IO_DEVICE}; IODEV_BIT1 = IO_DEVICE[1];
  //   IODEV_BIT0 = IO_DEVICE[2]; ADDR_MODE[2:0] = {ADDR0, ADDR1, ADDR2}; OP1 = IR[14]; OP_CODE[1:0] = IR[15:14];
  //   OP0 = IR[15]; nReset = Reset

  // Notes on the sheet:
  //   Clock: Hz: 50000
  //   Reset: default 1
  //   S-CPU - 16-bit TTL Processor
  //   Clock, Reset & Step Counter
  //   ALU & Accumulator
  //   Instruction Control Logic
  //   Step counter
  //   Registers
  //   Carry Flag Logic
  //   Indirect Addressing Logic
  //   MMIO Device Decoder
  //   Memory Interface
  //   contents of ROM (hex, n*v repeats v):
  //   6,4007,a70f,6,f00b,f00b,ffff,20ff,2100,2101,7fff,6,7014,bf0f,6
  //   ,670f,4006,a70f,f07c,f07c,6,701d,bf0f,6,670f,4006,a70f,f0b2,f0b2
  //   ,6,7026,bf0f,6,670f,4006,a70f,f0de,f0de,6,702f,bf0f,6,670f,4006
  //   ,a70f,f0f7,f0f7,6,7038,bf0f,6,670f,4006,a70f,f510,f510,6,7041
  //   ,bf0f,6,670f,4006,a70f,f10b,f10b,6,704a,bf0f,6,670f,4006,a70f
  //   ,f182,f182,6,7053,bf0f,6,670f,4006,a70f,f1a2,f1a2,6,705c,bf0f
  //   ,6,670f,4006,a70f,f1d9,f1d9,6,7065,bf0f,6,670f,4006,a70f,f47f,f47f
  //   ,6,706e,bf0f,6,670f,4006,a70f,f1fe,f1fe,6,7077,bf0f,6,670f,4006
  //   ,a70f,f4bc,f4bc,6,7001,a802,f07a,f07b,6,7005,3000,7005,3000,4006
  //   ,f084,f0a3,6,700a,a100,6,6100,3000,700a,3000,4006,f08f,f0a8,6
  //   ,4008,a102,6,7902,3000,700a,3000,4006,f09a,f0ad,6,670f,7001,a70f
  //   ,6,7f0f,a70b,e70b,e70b,6,7001,a801,f0a6,f0a7,6,7002,a801,f0ab
  //   ,f0ac,6,7003,a801,f0b0,f0b1,6,3000,7001,f0cf,6,700f,a101,6,2101
  //   ,6101,7001,f0d4,6,4009,a102,6,3902,6101,7001,f0d9,6,670f,7001
  //   ,a70f,6,7f0f,a70b,e70b,e70b,6,7004,a801,f0d2,f0d3,6,7005,a801
  //   ,f0d7,f0d8,6,7006,a801,f0dc,f0dd,6,7123,a100,6,6100,3000,7123
  //   ,3000,4006,f0e9,f0f2,6,670f,7001,a70f,6,7f0f,a70b,e70b,e70b,6
  //   ,7007,a801,f0f5,f0f6,f0f8,f0fe,6,7008,a801,f0fc,f0fd,6,3000,7001
  //   ,f0f9,6,670f,7001,a70f,6,7f0f,a70b,e70b,e70b,6,700f,3010,3000
  //   ,a700,3000,701f,3000,4006,f116,f17d,6,6700,3000,3000,3000,701f
  //   ,3000,4006,f120,f17d,6,7003,a100,6,6100,3000,3000,3000,7003,3000
  //   ,4006,f12d,f17d,6,7003,3000,3000,3000,7003,3000,4006,f137,f17d
  //   ,6,7006,a70b,3000,a70a,6,7003,3000,270a,3000,a70c,6,670b,3003
  //   ,3000,3000,a70a,6,670c,3000,270a,3000,7005,3000,4006,f152,f17d
  //   ,6,7003,a700,3000,a100,6,6700,3000,a70a,6,7003,3000,270a,3000,3000
  //   ,6100,3000,4006,f166,f17d,6,700f,3000,a70a,6,700a,3000,270a,3000
  //   ,700a,3000,4006,f174,f17d,6,670f,7001,a70f,6,7f0f,a70b,e70b,e70b
  //   ,6,7009,a801,f180,f181,6,7001,7001,4006,3000,7001,3000,4006,f18c
  //   ,f19d,6,7003,3000,7001,7003,4006,f194,f19d,6,670f,7001,a70f,6
  //   ,7f0f,a70b,e70b,e70b,6,700a,a801,f1a0,f1a1,6,7055,bf0f,6,670f
  //   ,4006,a70f,6,70aa,bf0f,6,670f,4006,a70f,6,670f,7001,a70f,6,7f0f
  //   ,a100,6,670f,7001,a70f,6,7f0f,3000,7055,3000,4006,f1c3,f1d4,6
  //   ,6100,3000,70aa,3000,4006,f1cb,f1d4,6,670f,7001,a70f,6,7f0f,a70b
  //   ,e70b,e70b,6,700b,a801,f1d7,f1d8,f1e0,f1e0,6,700c,a801,f1de,f1df
  //   ,6,7001,a700,4006,f1f0,6,6700,6,a700,4006,f1ec,f1f0,6,6700,4006
  //   ,f1f5,6,700c,a801,f1f3,f1f4,6,670f,7001,a70f,6,7f0f,a70b,e70b,e70b
  //   ,6,7001,a70a,670a,a700,3000,7002,3000,4006,f209,f479,6,6700,f20c
  //   ,a70a,670a,f210,7001,7000,a700,3000,7004,3000,4006,f218,f479,6
  //   ,6700,f21b,a70a,670a,f21f,7001,7000,a70a,670a,f224,7001,7000,a70a
  //   ,670a,f229,7001,7000,a70a,670a,f22e,7001,7000,a70a,670a,f233,7001
  //   ,7000,a70a,670a,f238,7001,7000,a70a,670a,f23d,7001,7000,a70a,670a
  //   ,f242,7001,7000,a70a,670a,f247,7001,7000,a70a,670a,f24c,7001,7000
  //   ,a70a,670a,f251,7001,7000,a70a,670a,f256,7001,7000,a70a,670a,f25b
  //   ,7001,7000,a70a,670a,f260,7001,7000,a70a,670a,f265,7001,7000,a700
  //   ,3000,7002,3000,4006,f26d,f479,6,6700,a70a,670a,f273,7001,7000
  //   ,a70a,670a,f278,7001,7000,a70a,670a,f27d,7001,7000,a70a,670a,f282
  //   ,7001,7000,a70a,670a,f287,7001,7000,a70a,670a,f28c,7001,7000,a70a
  //   ,670a,f291,7001,7000,a70a,670a,f296,7001,7000,a70a,670a,f29b,7001
  //   ,7000,a70a,670a,f2a0,7001,7000,a70a,670a,f2a5,7001,7000,a70a,670a
  //   ,f2aa,7001,7000,a70a,670a,f2af,7001,7000,a70a,670a,f2b4,7001,7000
  //   ,a70a,670a,f2b9,7001,7000,3000,a70a,6,400a,3000,270a,3000,7001
  //   ,3000,4006,f2c6,f479,6,7003,a70a,670a,f2cc,7001,7000,a70a,670a
  //   ,f2d1,7001,7000,a70a,670a,f2d6,7001,7000,a70a,670a,f2db,7001,7000
  //   ,a70a,670a,f2e0,7001,7000,a70a,670a,f2e5,7001,7000,a70a,670a,f2ea
  //   ,7001,7000,a70a,670a,f2ef,7001,7000,a70a,670a,f2f4,7001,7000,a70a
  //   ,670a,f2f9,7001,7000,a70a,670a,f2fe,7001,7000,a70a,670a,f303,7001
  //   ,7000,a70a,670a,f308,7001,7000,a70a,670a,f30d,7001,7000,a70a,670a
  //   ,f312,7001,7000,3000,a70a,6,400a,3000,270a,3000,7001,3000,4006
  //   ,f31f,f479,6,447e,a70a,670a,f325,7001,7000,a70a,670a,f32a,7001
  //   ,7000,a70a,670a,f32f,7001,7000,a70a,670a,f334,7001,7000,a700,3000
  //   ,7003,3000,4006,f33c,f479,6,6700,a70a,670a,f342,7001,7000,a70a
  //   ,670a,f347,7001,7000,a70a,670a,f34c,7001,7000,a70a,670a,f351,7001
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  //   Instruction Signal Routing
  //   Memory-Mapped I/O Devices
  //   Device 0 / Register 1 : HEX Display (0x12801)
  //   Device 0 / Register 2 : LED bank (0x12802)
  //   Device 1 - TTY
  //   Device 3 - Inputs Interface
endmodule
