// Digital circuit TerminalDevice.dig as structural Verilog
module TerminalDevice (
  input  Reset,
  input  [15:0] D_In,
  input  Clock,
  input  DO_STA,
  input  [15:0] IR_BIT0,
  input  nEnable,
  input  [15:0] IR_BIT1,
  output [15:0] D_OUT
);

  wire _7404_1_p9, _7404_1_p10, _7404_1_p11, _7408_1_p5, _7408_1_p8, _7408_1_p10, _7408_1_p13, _7408_2_p3,
       _7408_2_p11, _7432_1_pin4, _7432_1_pin5, _7432_1_pin9, _7432_1_pin10, _7432_1_pin12, _7432_1_pin13,
       Enable, KB_ACTIVE, KB_AVAI, KB_DATA, nIR_BIT0, notconnected_1_out, notconnected_2_out;
  wire [0:0] keyboard_1_av;
  wire [15:0] keyboard_1_d, multiplexer_1_out;

  // NotConnected on notconnected_1_out
  // NotConnected on notconnected_2_out
  // _7408 _7408_1: pin names not known; wires that end beside it: notconnected_1_out, notconnected_2_out, Enable, DO_STA, _7408_1_p5, 1'b0, 1'b1, _7408_1_p8, IR_BIT0, _7408_1_p10, _7408_1_p10, _7408_1_p5, _7408_1_p13
  // _7404 _7404_1: pin names not known; wires that end beside it: IR_BIT1, _7408_1_p8, IR_BIT0, nIR_BIT0, nEnable, Enable, 1'b0, 1'b1, _7404_1_p9, _7404_1_p10, _7404_1_p11
  Terminal terminal_1 (.D(D_In), .C(Clock), .en(_7408_1_p13));
  Keyboard keyboard_1 (.C(Clock), .en(KB_ACTIVE), .D(keyboard_1_d), .av(keyboard_1_av[0]));
  // NotConnected on _7404_1_p9
  // NotConnected on _7404_1_p10
  // NotConnected on _7404_1_p11
  // _7408 _7408_2: pin names not known; wires that end beside it: Enable, nIR_BIT0, _7408_2_p3, _7408_2_p3, IR_BIT1, KB_DATA, 1'b0, 1'b1, Enable, IR_BIT0, _7408_2_p11, _7408_2_p11, IR_BIT1, KB_AVAI
  Multiplexer #(.Bits(16)) multiplexer_1 (
    .sel(KB_AVAI), .in_0(keyboard_1_d), .in_1({{15{1'b0}}, keyboard_1_av[0]}), .out(multiplexer_1_out));
  assign D_OUT = KB_ACTIVE ? multiplexer_1_out : 16'bz;  // Driver driver_1
  _7432 _7432_1 (
    .pin1(KB_AVAI), .pin2(KB_DATA), .pin3(KB_ACTIVE), .pin4(_7432_1_pin4), .pin5(_7432_1_pin5), .pin7(1'b0),
    .pin9(_7432_1_pin9), .pin10(_7432_1_pin10), .pin12(_7432_1_pin12), .pin13(_7432_1_pin13), .pin14(1'b1));  // open: pin6, pin8, pin11
  // NotConnected on _7432_1_pin4
  // NotConnected on _7432_1_pin5
  // NotConnected on _7432_1_pin13
  // NotConnected on _7432_1_pin12
  // NotConnected on _7432_1_pin10
  // NotConnected on _7432_1_pin9

  // Other names for the same wires on the sheet: DATA_IN[15:0] = D_In; DATA_OUT[15:0] = D_OUT

  // Notes on the sheet:
  //   Clock: Hz: 10
endmodule
