// Logisim project SCPU.circ as structural Verilog: 1 circuit, main circuit Main
module Main (
  input  Reset
);

  wire ACCU_WE, and_10_out, and_15_out, and_16_out, and_17_out, and_18_out, and_19_out, and_21_out,
       and_22_out, and_23_out, and_24_out, and_25_out, and_26_out, and_27_out, and_28_out, CARRY, CARRY_RST,
       CARRY_WE, CF_ADDR, CLK, DEVICE0, DEVICE1, DEVICE_SCPU, DO_JMP, DO_STA, EXT_IO, FETCH_IR, FLAG_C,
       IMMEDIATE, INDIRECTED, INDIRECTION, not_2_out, OP_ADD, OP_JMP, OP_NOR, OP_STA, or_2_out, or_3_out,
       or_4_out, RAM_OE, ROM_OE, S0, S1;
  wire [0:0] keyboard_1_avail;
  wire [2:0] ADDR_MODE, IO_DEVICE;
  wire [3:0] register_6_q;
  wire [6:0] keyboard_1_data;
  wire [15:0] Accu, adder_1_out, ALU_OP, ALUR, DataBus, IR, NEXT_IR, nor_1_out, PC, ram_1_dout, ram_2_dout,
       register_5_q, ROM_ADDR;

  Counter #(.max('hffff), .width(16)) counter_1 (
    .clr(Reset), .load(DO_JMP), .up(1'b1), .count(FETCH_IR), .clk(CLK), .D(ALU_OP), .Q(PC));  // open: carry
  Counter #(.max('h1), .width(1)) counter_2 (
    .clr(Reset), .up(1'b1), .count(1'b1), .clk(CLK), .Q(S1));  // open: load, D, carry
  Clock clock_1 (.out(CLK));
  // Probe on PC
  // Probe on {IR[15:14], ADDR_MODE, IO_DEVICE, IR[7:0]}
  // Probe on Accu
  // Probe on DataBus
  and and_1 (FETCH_IR, S0, ~INDIRECTED);  // AND_Gate
  not not_1 (S0, S1);
  Register #(.width(16)) register_1 (
    .D(NEXT_IR), .en(S0), .clk(CLK), .Q({IR[15:14], ADDR_MODE, IO_DEVICE, IR[7:0]}), .clr(Reset));
  and and_2 (DEVICE_SCPU, IO_DEVICE[0], IO_DEVICE[1], IO_DEVICE[2], EXT_IO);
  // Probe on {IR[15:14], ADDR_MODE, IO_DEVICE, IR[7:0]}
  and and_3 (OP_NOR, ~IR[14], ~IR[15], ~INDIRECTION);  // AND_Gate
  and and_4 (OP_ADD, IR[14], ~IR[15], ~INDIRECTION);  // AND_Gate
  and and_5 (OP_STA, ~IR[14], IR[15], ~INDIRECTION);  // AND_Gate
  and and_6 (OP_JMP, IR[14], IR[15], ~INDIRECTION);  // AND_Gate
  or or_1 (ROM_OE, ~ADDR_MODE[2], FETCH_IR);  // OR_Gate
  and and_7 (IMMEDIATE, ~ADDR_MODE[0], ADDR_MODE[1], ADDR_MODE[2]);  // AND_Gate
  and and_8 (INDIRECTION, ADDR_MODE[0], ADDR_MODE[1], ADDR_MODE[2]);
  and and_9 (EXT_IO, ADDR_MODE[0], ~ADDR_MODE[1], ADDR_MODE[2], ~S0);  // AND_Gate
  and and_10 (and_10_out, ~ADDR_MODE[0], ~ADDR_MODE[1], ADDR_MODE[2]);  // AND_Gate
  or or_2 (or_2_out, and_10_out, INDIRECTION);
  and and_11 (RAM_OE, or_2_out, ~FETCH_IR);  // AND_Gate
  Register #(.width(16)) register_2 (.D(ALUR), .en(ACCU_WE), .clk(CLK), .Q(Accu), .clr(Reset));
  or or_3 (or_3_out, OP_NOR, OP_ADD);
  Multiplexer #(.width(16)) multiplexer_1 (
    .in0({{5{1'b0}}, IO_DEVICE, IR[7:0]}), .in1(DataBus), .out(ALU_OP), .sel(not_2_out));
  not not_2 (not_2_out, IMMEDIATE);
  and and_12 (ACCU_WE, S1, or_3_out);
  and and_13 (CF_ADDR, DEVICE_SCPU, IR[0], IR[1], IR[2], IR[3]);
  and and_14 (DO_STA, S1, OP_STA);
  Register #(.width(1)) register_3 (.D(1'b1), .en(and_15_out), .clk(CLK), .Q(INDIRECTED), .clr(and_16_out));
  and and_15 (and_15_out, S1, INDIRECTION);
  // Probe on NEXT_IR
  Multiplexer #(.width(16)) multiplexer_2 (
    .in0(DataBus), .in1({IR[15:14], DataBus[13:0]}), .out(NEXT_IR), .sel(INDIRECTION));
  and and_16 (and_16_out, S1, INDIRECTED);
  assign nor_1_out = ~(Accu | ALU_OP);  // NOR_Gate nor_1, 16 bits wide
  Adder #(.width(16)) adder_1 (.a(Accu), .b(ALU_OP), .out(adder_1_out), .cout(FLAG_C));  // open: cin
  Register #(.width(1)) register_4 (.D(or_4_out), .en(CARRY_WE), .clk(CLK), .Q(CARRY), .clr(CARRY_RST));
  or or_4 (or_4_out, CF_ADDR, FLAG_C);
  and and_17 (and_17_out, S1, OP_ADD);
  and and_18 (and_18_out, DO_STA, CF_ADDR);
  and and_19 (and_19_out, S0, OP_JMP);
  and and_20 (DO_JMP, S1, OP_JMP, ~CARRY);  // AND_Gate
  Multiplexer #(.width(16)) multiplexer_3 (.in0(nor_1_out), .in1(adder_1_out), .out(ALUR), .sel(OP_ADD));
  or or_5 (CARRY_WE, and_17_out, and_18_out);
  or or_6 (CARRY_RST, Reset, and_19_out);
  RAM #(.addrWidth(16), .dataWidth(16), .enables("line"), .\type ("nonvolatile")) ram_1 (
    .addr(ROM_ADDR), .we(1'b0), .clk(CLK), .din(Accu), .dout(ram_1_dout));
  RAM #(.addrWidth(16), .dataWidth(16), .enables("line")) ram_2 (
    .addr({{5{1'b0}}, IO_DEVICE, IR[7:0]}), .we(and_21_out), .clk(CLK), .din(Accu), .dout(ram_2_dout));
  and and_21 (and_21_out, RAM_OE, DO_STA);
  // Probe on ROM_ADDR
  Multiplexer #(.width(16)) multiplexer_4 (
    .in0({3'b000, ADDR_MODE[1:0], IO_DEVICE, IR[7:0]}), .in1(PC), .out(ROM_ADDR), .sel(S0));
  assign DataBus = ROM_OE ? ram_1_dout : 16'bz;  // Controlled_Buffer controlled_buffer_1
  assign DataBus = RAM_OE ? ram_2_dout : 16'bz;  // Controlled_Buffer controlled_buffer_2
  and and_22 (and_22_out, DO_STA, DEVICE0);
  and and_23 (and_23_out, DO_STA, DEVICE1);
  and and_24 (and_24_out, IR[0], ~IR[1], and_22_out);  // AND_Gate
  and and_25 (and_25_out, and_22_out, ~IR[0], IR[1]);  // AND_Gate
  TTY tty_1 (.data(Accu[6:0]), .clk(CLK), .we(and_26_out), .clr(Reset));
  and and_26 (and_26_out, IR[0], ~IR[1], and_23_out);  // AND_Gate
  and and_27 (and_27_out, DEVICE1, ~IR[0], IR[1]);  // AND_Gate
  and and_28 (and_28_out, DEVICE1, IR[0], IR[1]);
  and and_29 (DEVICE0, ~IO_DEVICE[0], ~IO_DEVICE[1], ~IO_DEVICE[2], EXT_IO);  // AND_Gate
  Register #(.width(16)) register_5 (.D(Accu), .en(and_24_out), .clk(CLK), .Q(register_5_q), .clr(Reset));
  Register #(.width(4)) register_6 (.D(Accu[3:0]), .en(and_25_out), .clk(CLK), .Q(register_6_q), .clr(Reset));
  Keyboard keyboard_1 (.clk(CLK), .re(and_27_out), .clr(Reset), .avail(keyboard_1_avail[0]), .data(keyboard_1_data));
  // LedBar #(.inputtype("row"), .matrixcols(4)) ledbar_1: pin names not known; wires that end beside it: register_6_q
  and and_30 (DEVICE1, IO_DEVICE[0], ~IO_DEVICE[1], ~IO_DEVICE[2], EXT_IO);  // AND_Gate
  Hex_Digit_Display hex_digit_display_1 (.value(register_5_q[15:12]));  // open: dp
  assign DataBus = and_27_out ? {{9{1'b0}}, keyboard_1_data} : 16'bz;  // Controlled_Buffer controlled_buffer_3
  assign DataBus = and_28_out ? {{15{1'b0}}, keyboard_1_avail[0]} : 16'bz;  // Controlled_Buffer controlled_buffer_4
  Hex_Digit_Display hex_digit_display_2 (.value(register_5_q[11:8]));  // open: dp
  Hex_Digit_Display hex_digit_display_3 (.value(register_5_q[7:4]));  // open: dp
  Hex_Digit_Display hex_digit_display_4 (.value(register_5_q[3:0]));  // open: dp

  // Other names for the same wires on the sheet: OPCODE[1:0] = IR[15:14]; IR[13:8] = {ADDR_MODE, IO_DEVICE}

  // Notes on the sheet:
  //   Inputs
  //   Monitoring
  //   Program Counter
  //   Step counter
  //   Step 1 : Fetch instruction (S0)
  //   Instruction register
  //   Opcode & Address Modes
  //   Opcode Decoder
  //   Control Logic
  //   ALU Operand Selection
  //   Accumulator Register
  //   Step 2 : Execute instruction (S1)
  //   JMP / STA Control
  //   Indirect Addressing Logic
  //   ALU - NOR / ADD
  //   Carry Flag Register
  //   ROM address
  //   ROM
  //   MX29LV160D (1M x 16 BIT)
  //   RAM
  //   AS6C2016 (128K x 16 BIT)
  //   Device #0 — Display & LED Output
  //   0x2801
  //   0x2802
  //   Device #1 : TTY Console
  //   0x2901
  //   0x2902
  //   0x2903
endmodule
